# Fritzing sketch register2 (saved by Fritzing 0.9.4)
breadboards: 1

parts:
  IC6 = IC, DIP package, 20 pins [chip_label=377]
  IC7 = IC, DIP package, 20 pins [chip_label=245]
  IC8 = IC, DIP package, 20 pins [chip_label=245]
  IC5 = IC, DIP package, 20 pins [chip_label=377]

nets:
  N1: IC6.pin1, IC5.pin1
  N2: IC6.pin2, IC7.pin15
  N3: IC6.pin3, IC6.pin4
  N4: IC6.pin5, IC7.pin17
  N5: IC6.pin6, IC7.pin11
  N6: IC6.pin7, IC6.pin8
  N7: IC6.pin9, IC7.pin13
  N8: IC6.pin10, IC7.pin1, IC7.pin10, IC8.pin1, IC8.pin10, IC5.pin10
  N9: IC6.pin11, IC5.pin11
  N10: IC6.pin12, IC7.pin14
  N11: IC6.pin13, IC6.pin14
  N12: IC6.pin15, IC7.pin12
  N13: IC6.pin16, IC7.pin18
  N14: IC6.pin17, IC6.pin18
  N15: IC6.pin19, IC7.pin16
  N16: IC6.pin20, IC7.pin20, IC8.pin20, IC5.pin20
  N17: IC7.pin2, IC7.pin9
  N18: IC7.pin19, IC8.pin19
  N19: IC8.pin2, IC8.pin9
  N20: IC8.pin11, IC5.pin15
  N21: IC8.pin12, IC5.pin6
  N22: IC8.pin13, IC5.pin12
  N23: IC8.pin14, IC5.pin9
  N24: IC8.pin15, IC5.pin19
  N25: IC8.pin16, IC5.pin2
  N26: IC8.pin17, IC5.pin16
  N27: IC8.pin18, IC5.pin5
  N28: IC5.pin3, IC5.pin4
  N29: IC5.pin7, IC5.pin8
  N30: IC5.pin13, IC5.pin14
  N31: IC5.pin17, IC5.pin18

notes:
  W
  OE
  CLK
