# Fritzing sketch register_control (saved by Fritzing 0.9.4)
breadboards: 4

parts:
  IC9 = IC, DIP package, 20 pins [chip_label=377]
  IC10 = IC, DIP package, 20 pins [chip_label=377]
  IC11 = IC, DIP package, 20 pins [chip_label=245]
  IC12 = IC, DIP package, 20 pins [chip_label=245]
  IC13 = IC, DIP package, 20 pins [chip_label=BUF]  # not connected
  IC14 = IC, DIP package, 16 pins [chip_label=ADD]  # not connected
  IC15 = IC, DIP package, 16 pins [chip_label=ADD]  # not connected
  IC16 = IC, DIP package, 16 pins [chip_label=MUX]  # not connected
  IC17 = IC, DIP package, 16 pins [chip_label=MUX]  # not connected
  IC18 = IC, DIP package, 16 pins [chip_label=MUX]  # not connected
  IC19 = IC, DIP package, 16 pins [chip_label=MUX]  # not connected
  IC20 = IC, DIP package, 16 pins [chip_label=ADD]  # not connected
  IC21 = IC, DIP package, 16 pins [chip_label=ADD]  # not connected
  IC22 = IC, DIP package, 20 pins [chip_label=BUF]  # not connected
  IC23 = IC, DIP package, 20 pins [chip_label=BUF]  # not connected
  IC25 = IC, DIP package, 16 pins [chip_label=DEMUX]  # not connected
  IC26 = IC, DIP package, 16 pins [chip_label=DEMUX]  # not connected
  IC27 = IC, DIP package, 20 pins [chip_label=BUF]  # not connected
  IC28 = IC, DIP package, 20 pins [chip_label=BUF]  # not connected
  IC29 = IC, DIP package, 20 pins [chip_label=BUF]
  IC30 = IC, DIP package, 14 pins [chip_label=XOR]  # not connected

nets:
  N1: IC9.pin1, IC10.pin1
  N2: IC9.pin2, IC11.pin16
  N3: IC9.pin3, IC9.pin4
  N4: IC9.pin5, IC11.pin18
  N5: IC9.pin6, IC11.pin12
  N6: IC9.pin7, IC9.pin8
  N7: IC9.pin9, IC11.pin14
  N8: IC9.pin10, IC10.pin10, IC11.pin1, IC11.pin10, IC12.pin1, IC12.pin10
  N9: IC9.pin11, IC10.pin11
  N10: IC9.pin12, IC11.pin13
  N11: IC9.pin13, IC9.pin14
  N12: IC9.pin15, IC11.pin11
  N13: IC9.pin16, IC11.pin17
  N14: IC9.pin17, IC9.pin18
  N15: IC9.pin19, IC11.pin15
  N16: IC9.pin20, IC10.pin20, IC11.pin20, IC12.pin20
  N17: IC10.pin2, IC12.pin15
  N18: IC10.pin5, IC12.pin17
  N19: IC10.pin6, IC12.pin11
  N20: IC10.pin9, IC12.pin13
  N21: IC10.pin12, IC12.pin14
  N22: IC10.pin13, IC10.pin14
  N23: IC10.pin15, IC12.pin12
  N24: IC10.pin16, IC12.pin18
  N25: IC10.pin17, IC10.pin18
  N26: IC10.pin19, IC12.pin16
  N27: IC11.pin2, IC11.pin9
  N28: IC11.pin19, IC12.pin19
  N29: IC12.pin2, IC12.pin9, IC29.pin2, IC29.pin9
  N30: IC12.pin3, IC29.pin3
  N31: IC12.pin4, IC29.pin4
  N32: IC12.pin5, IC29.pin5
  N33: IC12.pin6, IC29.pin6
  N34: IC12.pin7, IC29.pin7
  N35: IC12.pin8, IC29.pin8
  N36: IC29.pin1, IC29.pin10

notes:
  W
  OE
  CLK
